// Logisim project Main bus.circ as structural Verilog: 1 circuit, main circuit Main bus
module Main_bus (
  input  in_1
);

  wire AccBuf, ALUBuf, decoder_1_out2, decoder_1_out3, decoder_1_out4, decoder_1_out5, decoder_1_out7,
       ExOnes, IBuf, IRBuf, Jump, MARBuf, nor_1_out, not_1_out, OBuf, PCBuf, PCEn, RAMRead, RAMWrite, RegBuf;
  wire [1:0] priority_encoder_1_out;
  wire [2:0] ALU, Phase;
  wire [15:0] Accumulator_register_q, alu_1_out_4, bit_extender_1_out, bit_extender_2_out,
       controlled_buffer_1_out, controlled_buffer_2_out, controlled_buffer_4_out, controlled_buffer_5_out,
       controlled_buffer_7_out, controlled_buffer_9_out, controlled_buffer_11_out, Input_register_q,
       InstrData, Instruction_register_q, Memory_access_register_q, multiplexer_2_out, Output_register_q,
       Program_counter_q, ram_1_data, rom_1_data;

  Register #(.width(16)) Memory_access_register (
    .D(controlled_buffer_2_out), .en(1'b1), .Q(Memory_access_register_q), .clk(in_1));  // open: clr
  Register #(.width(16)) Instruction_register (
    .D(controlled_buffer_5_out), .en(1'b1), .Q(Instruction_register_q), .clk(in_1));  // open: clr
  Decoder #(.select(3)) decoder_1 (
    .out0(PCBuf), .out1(IRBuf), .out2(decoder_1_out2), .out3(decoder_1_out3), .out4(decoder_1_out4),
    .out5(decoder_1_out5), .out6(PCEn), .out7(decoder_1_out7), .sel(Phase), .en(1'b1));
  assign bit_extender_1_out = {{4{1'b0}}, Instruction_register_q[11:0]};  // Bit_Extender bit_extender_1
  assign bit_extender_2_out = {{4{1'b1}}, Instruction_register_q[11:0]};  // Bit_Extender bit_extender_2
  Priority_Encoder #(.select(2), .disabled(0)) priority_encoder_1 (
    .in0(decoder_1_out2), .in1(decoder_1_out3), .in2(decoder_1_out4), .in3(decoder_1_out5),
    .out(priority_encoder_1_out), .en_in(nor_1_out));  // open: gs, en_out
  nor nor_1 (nor_1_out, PCEn, PCBuf, IRBuf);
  Counter #(.width(16), .max('hffff)) Program_counter (
    .load(Jump), .D(InstrData), .count(PCEn), .Q(Program_counter_q), .clk(in_1));  // open: carry, clr
  RAM #(.addrWidth(16), .dataWidth(16), .bus("separate")) ram_1 (
    .addr(Memory_access_register_q), .din(controlled_buffer_4_out), .data(ram_1_data), .str(RAMWrite),
    .clk(in_1), .ld(1'b1));  // open: sel, clr
  Multiplexer #(.width(16)) multiplexer_1 (
    .in0(bit_extender_1_out), .in1(bit_extender_2_out), .out(InstrData), .sel(ExOnes), .en(1'b1));
  Clock clock_1 ();  // open: out
  Counter #(.width(3), .max('h6)) counter_1 (.count(1'b1), .Q(Phase), .clk(in_1));  // open: load, D, carry, clr
  assign controlled_buffer_1_out = PCBuf ? Program_counter_q : 16'bz;  // Controlled_Buffer controlled_buffer_1
  assign controlled_buffer_2_out = MARBuf ? controlled_buffer_1_out : 16'bz;  // Controlled_Buffer controlled_buffer_2
  assign controlled_buffer_1_out = RAMRead ? ram_1_data : 16'bz;  // Controlled_Buffer controlled_buffer_3
  assign controlled_buffer_4_out = RAMWrite ? controlled_buffer_1_out : 16'bz;  // Controlled_Buffer controlled_buffer_4
  assign controlled_buffer_5_out = IRBuf ? controlled_buffer_1_out : 16'bz;  // Controlled_Buffer controlled_buffer_5
  ROM #(.addrWidth(6), .dataWidth(16)) rom_1 (
    .addr({Instruction_register_q[15:12], priority_encoder_1_out}), .data(rom_1_data));  // open: sel
  Multiplexer #(.width(16)) multiplexer_2 (
    .in0({16{1'b0}}), .in1(rom_1_data),
    .out({multiplexer_2_out[15:10], ExOnes, Jump, IBuf, OBuf, AccBuf, RegBuf, ALUBuf, RAMWrite, multiplexer_2_out[1:0]}),
    .sel(nor_1_out));  // open: en
  assign controlled_buffer_1_out = ALUBuf ? Accumulator_register_q : 16'bz;  // Controlled_Buffer controlled_buffer_6
  not not_1 (not_1_out, AccBuf);
  assign controlled_buffer_7_out = not_1_out ? alu_1_out_4 : 16'bz;  // Controlled_Buffer controlled_buffer_7
  assign controlled_buffer_7_out = AccBuf ? controlled_buffer_1_out : 16'bz;  // Controlled_Buffer controlled_buffer_8
  assign controlled_buffer_9_out = RegBuf ? controlled_buffer_1_out : 16'bz;  // Controlled_Buffer controlled_buffer_9
  assign controlled_buffer_1_out = IBuf ? InstrData : 16'bz;  // Controlled_Buffer controlled_buffer_10
  assign controlled_buffer_11_out = OBuf ? controlled_buffer_1_out : 16'bz;  // Controlled_Buffer controlled_buffer_11
  Register #(.width(16)) Input_register (
    .D(controlled_buffer_9_out), .en(1'b1), .Q(Input_register_q), .clk(in_1));  // open: clr
  Hex_Digit_Display hex_digit_display_1 (.value(Output_register_q[15:12]));  // open: dp
  Register #(.width(16)) Output_register (
    .D(controlled_buffer_11_out), .en(1'b1), .Q(Output_register_q), .clk(in_1));  // open: clr
  Register #(.width(16)) Accumulator_register (
    .D(controlled_buffer_7_out), .en(1'b1), .Q(Accumulator_register_q), .clk(in_1));  // open: clr
  Hex_Digit_Display hex_digit_display_2 (.value(Output_register_q[11:8]));  // open: dp
  Hex_Digit_Display hex_digit_display_3 (.value(Output_register_q[7:4]));  // open: dp
  Bit_Extender #(.in_width(6), .out_width(3)) bit_extender_3 (.in(multiplexer_2_out[15:10]), .out(ALU));
  ALU alu_1 (.in_1(Accumulator_register_q), .in_2(Input_register_q), .out_4(alu_1_out_4), .in_3(ALU));
  Hex_Digit_Display hex_digit_display_4 (.value(Output_register_q[3:0]));  // open: dp
  or or_1 (MARBuf, PCBuf, multiplexer_2_out[0]);
  or or_2 (RAMRead, IRBuf, multiplexer_2_out[1]);

  // Other names for the same wires on the sheet: clk = in_1

  // Notes on the sheet:
  //   Address 0000-EFFF: Program
  //   Address F000-FFFF: Data
  //   B0 is the opcode
  //   B1/2/3 are data
  //   contents of rom_1 (hex, n*v repeats v):
  //   4*0 281 22 0 0 4*2222 4*3333 4*4444 4*5555 4*6666 4*7777 4*8888 4*9999 4*aaaa 4*bbbb 4*cccc 4*dddd
  //   4*eeee 4*ffff
  //   OPCODE 0x0: NOP >> NOP >> NOP >> NOP
  //   OPCODE 0x1:  load address into MAR >> load memory value into accumulator >> NOP >> NOP
endmodule
