// Logisim project Program counter.circ as structural Verilog: 2 circuits, main circuit Program counter
module Program_counter (
  input  Count_enable,
  input  [15:0] Count_input,
  input  Clear,
  output [15:0] Count_output
);

  wire and_1_out, and_2_out, and_3_out, and_4_out, and_5_out, and_6_out, and_7_out, and_8_out, and_9_out,
       and_10_out, and_11_out, and_12_out, and_13_out, and_14_out, and_15_out, clock_1_out;

  and and_1 (and_1_out, Count_enable, Count_output[0]);
  and and_2 (and_2_out, Count_output[2], and_3_out);
  Clock clock_1 (.out(clock_1_out));
  and and_3 (and_3_out, and_1_out, Count_output[1]);
  J_K_Flip_Flop j_k_ff_1 (
    .J(Count_enable), .clk(clock_1_out), .K(Count_enable), .Q(Count_output[0]), .preset(Count_input[0]),
    .reset(Clear));  // open: Qn, en
  J_K_Flip_Flop j_k_ff_2 (
    .J(and_1_out), .clk(clock_1_out), .K(and_1_out), .Q(Count_output[1]), .preset(Count_input[1]),
    .reset(Clear));  // open: Qn, en
  J_K_Flip_Flop j_k_ff_3 (
    .J(and_3_out), .clk(clock_1_out), .K(and_3_out), .Q(Count_output[2]), .preset(Count_input[2]),
    .reset(Clear));  // open: Qn, en
  J_K_Flip_Flop j_k_ff_4 (
    .J(and_2_out), .clk(clock_1_out), .K(and_2_out), .Q(Count_output[3]), .preset(Count_input[3]),
    .reset(Clear));  // open: Qn, en
  and and_4 (and_4_out, and_2_out, Count_output[3]);
  and and_5 (and_5_out, Count_output[4], and_4_out);
  and and_6 (and_6_out, and_5_out, Count_output[5]);
  and and_7 (and_7_out, Count_output[6], and_6_out);
  J_K_Flip_Flop j_k_ff_5 (
    .J(and_4_out), .clk(clock_1_out), .K(and_4_out), .Q(Count_output[4]), .preset(Count_input[4]),
    .reset(Clear));  // open: Qn, en
  J_K_Flip_Flop j_k_ff_6 (
    .J(and_5_out), .clk(clock_1_out), .K(and_5_out), .Q(Count_output[5]), .preset(Count_input[5]),
    .reset(Clear));  // open: Qn, en
  J_K_Flip_Flop j_k_ff_7 (
    .J(and_6_out), .clk(clock_1_out), .K(and_6_out), .Q(Count_output[6]), .preset(Count_input[6]),
    .reset(Clear));  // open: Qn, en
  J_K_Flip_Flop j_k_ff_8 (
    .J(and_7_out), .clk(clock_1_out), .K(and_7_out), .Q(Count_output[7]), .preset(Count_input[7]),
    .reset(Clear));  // open: Qn, en
  and and_8 (and_8_out, and_7_out, Count_output[7]);
  and and_9 (and_9_out, Count_output[8], and_8_out);
  and and_10 (and_10_out, and_9_out, Count_output[9]);
  and and_11 (and_11_out, Count_output[10], and_10_out);
  J_K_Flip_Flop j_k_ff_9 (
    .J(and_8_out), .clk(clock_1_out), .K(and_8_out), .Q(Count_output[8]), .preset(Count_input[8]),
    .reset(Clear));  // open: Qn, en
  J_K_Flip_Flop j_k_ff_10 (
    .J(and_9_out), .clk(clock_1_out), .K(and_9_out), .Q(Count_output[9]), .preset(Count_input[9]),
    .reset(Clear));  // open: Qn, en
  J_K_Flip_Flop j_k_ff_11 (
    .J(and_10_out), .clk(clock_1_out), .K(and_10_out), .Q(Count_output[10]), .preset(Count_input[10]),
    .reset(Clear));  // open: Qn, en
  J_K_Flip_Flop j_k_ff_12 (
    .J(and_11_out), .clk(clock_1_out), .K(and_11_out), .Q(Count_output[11]), .preset(Count_input[11]),
    .reset(Clear));  // open: Qn, en
  and and_12 (and_12_out, and_11_out, Count_output[11]);
  and and_13 (and_13_out, Count_output[12], and_12_out);
  and and_14 (and_14_out, and_13_out, Count_output[13]);
  and and_15 (and_15_out, Count_output[14], and_14_out);
  J_K_Flip_Flop j_k_ff_13 (
    .J(and_12_out), .clk(clock_1_out), .K(and_12_out), .Q(Count_output[12]), .preset(Count_input[12]),
    .reset(Clear));  // open: Qn, en
  J_K_Flip_Flop j_k_ff_14 (
    .J(and_13_out), .clk(clock_1_out), .K(and_13_out), .Q(Count_output[13]), .preset(Count_input[13]),
    .reset(Clear));  // open: Qn, en
  J_K_Flip_Flop j_k_ff_15 (
    .J(and_14_out), .clk(clock_1_out), .K(and_14_out), .Q(Count_output[14]), .preset(Count_input[14]),
    .reset(Clear));  // open: Qn, en
  J_K_Flip_Flop j_k_ff_16 (
    .J(and_15_out), .clk(clock_1_out), .K(and_15_out), .Q(Count_output[15]), .preset(Count_input[15]),
    .reset(Clear));  // open: Qn, en
endmodule

module _4_Bit_counter (
  input  Clock,
  input  Clear,
  input  Enable_count,
  input  Load_data,
  input  [3:0] Data_input,
  output [3:0] Count_output,
  output Enable_carry
);

  wire and_1_out, and_2_out, and_3_out, and_5_out, and_6_out, and_7_out, and_8_out;

  and and_1 (and_1_out, Count_output[1], and_2_out);
  T_Flip_Flop t_ff_1 (
    .clk(Clock), .T(Enable_count), .Q(Count_output[0]), .preset(and_5_out), .reset(Clear));  // open: Qn, en
  T_Flip_Flop t_ff_2 (
    .clk(Clock), .T(and_2_out), .Q(Count_output[1]), .preset(and_6_out), .reset(Clear));  // open: Qn, en
  and and_2 (and_2_out, Enable_count, Count_output[0]);
  T_Flip_Flop t_ff_3 (
    .clk(Clock), .T(and_1_out), .Q(Count_output[2]), .preset(and_7_out), .reset(Clear));  // open: Qn, en
  and and_3 (and_3_out, and_1_out, Count_output[2]);
  T_Flip_Flop t_ff_4 (
    .clk(Clock), .T(and_3_out), .Q(Count_output[3]), .preset(and_8_out), .reset(Clear));  // open: Qn, en
  and and_4 (Enable_carry, and_3_out, Count_output[3]);
  and and_5 (and_5_out, Load_data, Data_input[3]);
  and and_6 (and_6_out, Load_data, Data_input[2]);
  and and_7 (and_7_out, Load_data, Data_input[1]);
  and and_8 (and_8_out, Load_data, Data_input[0]);
endmodule
