// Logisim project RAM.circ as structural Verilog: 8 circuits, main circuit RAM
module RAM (
  input  [3:0] Address,
  input  Enable
);

  wire undriven_33, undriven_34;
  wire [3:0] undriven_2, undriven_4, undriven_6, undriven_8, undriven_10, undriven_12, undriven_14,
       undriven_16, undriven_18, undriven_20, undriven_22, undriven_24, undriven_26, undriven_28,
       undriven_30, undriven_32;
  wire [15:0] n4x16_decoder_1_output;
  wire [19:0] n16_word_array_1_output, n16_word_array_2_output, n16_word_array_3_output,
       n16_word_array_4_output, n16_word_array_5_output, n16_word_array_6_output, n16_word_array_7_output,
       n16_word_array_8_output, n16_word_array_9_output, n16_word_array_10_output, n16_word_array_11_output,
       n16_word_array_12_output, n16_word_array_13_output, n16_word_array_14_output,
       n16_word_array_15_output, n16_word_array_16_output, undriven, undriven_3, undriven_5, undriven_7,
       undriven_9, undriven_11, undriven_13, undriven_15, undriven_17, undriven_19, undriven_21, undriven_23,
       undriven_25, undriven_27, undriven_29, undriven_31;

  _4x16_decoder u_4x16_decoder_1 (.Input(Address), .Enable(Enable), .Output(n4x16_decoder_1_output));
  _16_Word_array u_16_word_array_1 (
    .Data(undriven), .Address(undriven_2), .Enable(undriven_33), .R_W(undriven_34),
    .Output(n16_word_array_1_output));
  _16_Word_array u_16_word_array_2 (
    .Data(undriven_3), .Address(undriven_4), .Enable(undriven_33), .R_W(undriven_34),
    .Output(n16_word_array_2_output));
  _16_Word_array u_16_word_array_3 (
    .Data(undriven_5), .Address(undriven_6), .Enable(undriven_33), .R_W(undriven_34),
    .Output(n16_word_array_3_output));
  _16_Word_array u_16_word_array_4 (
    .Data(undriven_7), .Address(undriven_8), .Enable(undriven_33), .R_W(undriven_34),
    .Output(n16_word_array_4_output));
  _16_Word_array u_16_word_array_5 (
    .Data(undriven_9), .Address(undriven_10), .Enable(undriven_33), .R_W(undriven_34),
    .Output(n16_word_array_5_output));
  _16_Word_array u_16_word_array_6 (
    .Data(undriven_11), .Address(undriven_12), .Enable(undriven_33), .R_W(undriven_34),
    .Output(n16_word_array_6_output));
  _16_Word_array u_16_word_array_7 (
    .Data(undriven_13), .Address(undriven_14), .Enable(undriven_33), .R_W(undriven_34),
    .Output(n16_word_array_7_output));
  _16_Word_array u_16_word_array_8 (
    .Data(undriven_15), .Address(undriven_16), .Enable(undriven_33), .R_W(undriven_34),
    .Output(n16_word_array_8_output));
  _16_Word_array u_16_word_array_9 (
    .Data(undriven_17), .Address(undriven_18), .Enable(undriven_33), .R_W(undriven_34),
    .Output(n16_word_array_9_output));
  _16_Word_array u_16_word_array_10 (
    .Data(undriven_19), .Address(undriven_20), .Enable(undriven_33), .R_W(undriven_34),
    .Output(n16_word_array_10_output));
  _16_Word_array u_16_word_array_11 (
    .Data(undriven_21), .Address(undriven_22), .Enable(undriven_33), .R_W(undriven_34),
    .Output(n16_word_array_11_output));
  _16_Word_array u_16_word_array_12 (
    .Data(undriven_23), .Address(undriven_24), .Enable(undriven_33), .R_W(undriven_34),
    .Output(n16_word_array_12_output));
  _16_Word_array u_16_word_array_13 (
    .Data(undriven_25), .Address(undriven_26), .Enable(undriven_33), .R_W(undriven_34),
    .Output(n16_word_array_13_output));
  _16_Word_array u_16_word_array_14 (
    .Data(undriven_27), .Address(undriven_28), .Enable(undriven_33), .R_W(undriven_34),
    .Output(n16_word_array_14_output));
  _16_Word_array u_16_word_array_15 (
    .Data(undriven_29), .Address(undriven_30), .Enable(undriven_33), .R_W(undriven_34),
    .Output(n16_word_array_15_output));
  _16_Word_array u_16_word_array_16 (
    .Data(undriven_31), .Address(undriven_32), .Enable(undriven_33), .R_W(undriven_34),
    .Output(n16_word_array_16_output));
endmodule

module _16_Word_array (
  input  [19:0] Data,
  input  [3:0] Address,
  input  Enable,
  input  R_W,
  output [19:0] Output
);

  wire [15:0] n4x16_decoder_1_output;
  wire [19:0] or_1_out, or_2_out, or_3_out, or_4_out, word_1_output, word_2_output, word_3_output,
       word_4_output, word_5_output, word_6_output, word_7_output, word_8_output, word_9_output,
       word_10_output, word_11_output, word_12_output, word_13_output, word_14_output, word_15_output,
       word_16_output;

  _4x16_decoder u_4x16_decoder_1 (.Input(Address), .Enable(Enable), .Output(n4x16_decoder_1_output));
  Word word_1 (.Select(n4x16_decoder_1_output[0]), .R_W(R_W), .Data(Data), .Output(word_1_output));
  Word word_2 (.Select(n4x16_decoder_1_output[1]), .R_W(R_W), .Data(Data), .Output(word_2_output));
  Word word_3 (.Select(n4x16_decoder_1_output[2]), .R_W(R_W), .Data(Data), .Output(word_3_output));
  Word word_4 (.Select(n4x16_decoder_1_output[3]), .R_W(R_W), .Data(Data), .Output(word_4_output));
  Word word_5 (.Select(n4x16_decoder_1_output[4]), .R_W(R_W), .Data(Data), .Output(word_5_output));
  Word word_6 (.Select(n4x16_decoder_1_output[5]), .R_W(R_W), .Data(Data), .Output(word_6_output));
  Word word_7 (.Select(n4x16_decoder_1_output[6]), .R_W(R_W), .Data(Data), .Output(word_7_output));
  Word word_8 (.Select(n4x16_decoder_1_output[7]), .R_W(R_W), .Data(Data), .Output(word_8_output));
  Word word_9 (.Select(n4x16_decoder_1_output[8]), .R_W(R_W), .Data(Data), .Output(word_9_output));
  Word word_10 (.Select(n4x16_decoder_1_output[9]), .R_W(R_W), .Data(Data), .Output(word_10_output));
  Word word_11 (.Select(n4x16_decoder_1_output[10]), .R_W(R_W), .Data(Data), .Output(word_11_output));
  Word word_12 (.Select(n4x16_decoder_1_output[11]), .R_W(R_W), .Data(Data), .Output(word_12_output));
  Word word_13 (.Select(n4x16_decoder_1_output[12]), .R_W(R_W), .Data(Data), .Output(word_13_output));
  Word word_14 (.Select(n4x16_decoder_1_output[13]), .R_W(R_W), .Data(Data), .Output(word_14_output));
  Word word_15 (.Select(n4x16_decoder_1_output[14]), .R_W(R_W), .Data(Data), .Output(word_15_output));
  Word word_16 (.Select(n4x16_decoder_1_output[15]), .R_W(R_W), .Data(Data), .Output(word_16_output));
  assign or_1_out = word_1_output | word_2_output | word_3_output | word_4_output;  // OR_Gate or_1, 20 bits wide
  assign or_2_out = word_5_output | word_6_output | word_7_output | word_8_output;  // OR_Gate or_2, 20 bits wide
  assign or_3_out = word_9_output | word_10_output | word_11_output | word_12_output;  // OR_Gate or_3, 20 bits wide
  assign or_4_out = word_13_output | word_14_output | word_15_output | word_16_output;  // OR_Gate or_4, 20 bits wide
  assign Output = or_1_out | or_2_out | or_3_out | or_4_out;  // OR_Gate or_5, 20 bits wide
endmodule

module Word (
  input  [19:0] Data,
  input  Select,
  input  R_W,
  output [19:0] Output
);

  Memory_cell memory_cell_1 (.Select(Select), .Input(Data[19]), .Output(Output[19]), .R_W(R_W));
  Memory_cell memory_cell_2 (.Select(Select), .Input(Data[18]), .Output(Output[18]), .R_W(R_W));
  Memory_cell memory_cell_3 (.Select(Select), .Input(Data[17]), .Output(Output[17]), .R_W(R_W));
  Memory_cell memory_cell_4 (.Select(Select), .Input(Data[16]), .Output(Output[16]), .R_W(R_W));
  Memory_cell memory_cell_5 (.Select(Select), .Input(Data[15]), .Output(Output[15]), .R_W(R_W));
  Memory_cell memory_cell_6 (.Select(Select), .Input(Data[14]), .Output(Output[14]), .R_W(R_W));
  Memory_cell memory_cell_7 (.Select(Select), .Input(Data[13]), .Output(Output[13]), .R_W(R_W));
  Memory_cell memory_cell_8 (.Select(Select), .Input(Data[12]), .Output(Output[12]), .R_W(R_W));
  Memory_cell memory_cell_9 (.Select(Select), .Input(Data[11]), .Output(Output[11]), .R_W(R_W));
  Memory_cell memory_cell_10 (.Select(Select), .Input(Data[10]), .Output(Output[10]), .R_W(R_W));
  Memory_cell memory_cell_11 (.Select(Select), .Input(Data[9]), .Output(Output[9]), .R_W(R_W));
  Memory_cell memory_cell_12 (.Select(Select), .Input(Data[8]), .Output(Output[8]), .R_W(R_W));
  Memory_cell memory_cell_13 (.Select(Select), .Input(Data[7]), .Output(Output[7]), .R_W(R_W));
  Memory_cell memory_cell_14 (.Select(Select), .Input(Data[6]), .Output(Output[6]), .R_W(R_W));
  Memory_cell memory_cell_15 (.Select(Select), .Input(Data[5]), .Output(Output[5]), .R_W(R_W));
  Memory_cell memory_cell_16 (.Select(Select), .Input(Data[4]), .Output(Output[4]), .R_W(R_W));
  Memory_cell memory_cell_17 (.Select(Select), .Input(Data[3]), .Output(Output[3]), .R_W(R_W));
  Memory_cell memory_cell_18 (.Select(Select), .Input(Data[2]), .Output(Output[2]), .R_W(R_W));
  Memory_cell memory_cell_19 (.Select(Select), .Input(Data[1]), .Output(Output[1]), .R_W(R_W));
  Memory_cell memory_cell_20 (.Select(Select), .Input(Data[0]), .Output(Output[0]), .R_W(R_W));
endmodule

module _4x16_decoder (
  input  [3:0] Input,
  input  Enable,
  output [15:0] Output
);

  wire and_1_out, and_2_out, not_1_out;

  not not_1 (not_1_out, Input[3]);
  and and_1 (and_1_out, Enable, not_1_out);
  and and_2 (and_2_out, Enable, Input[3]);
  _3x8_decoder u_3x8_decoder_1 (.Enable(and_1_out), .Output(Output[7:0]), .Input(Input[2:0]));
  _3x8_decoder u_3x8_decoder_2 (.Enable(and_2_out), .Output(Output[15:8]), .Input(Input[2:0]));
endmodule

module _3x8_decoder (
  input  [2:0] Input,
  input  Enable,
  output [7:0] Output
);

  wire and_1_out, and_2_out, not_1_out;

  not not_1 (not_1_out, Input[2]);
  _2x4_decoder u_2x4_decoder_1 (
    .Input_a(Input[1]), .Input_b(Input[0]), .Output_0(Output[0]), .Output_1(Output[1]), .Output_2(Output[2]),
    .Output_3(Output[3]), .Enable(and_1_out));
  and and_1 (and_1_out, Enable, not_1_out);
  _2x4_decoder u_2x4_decoder_2 (
    .Input_a(Input[1]), .Input_b(Input[0]), .Output_0(Output[4]), .Output_1(Output[5]), .Output_2(Output[6]),
    .Output_3(Output[7]), .Enable(and_2_out));
  and and_2 (and_2_out, Enable, Input[2]);
endmodule

module _2x4_decoder (
  input  Input_a,
  input  Input_b,
  input  Enable,
  output Output_0,
  output Output_1,
  output Output_2,
  output Output_3
);

  wire not_1_out, not_2_out;

  not not_1 (not_1_out, Input_a);
  not not_2 (not_2_out, Input_b);
  and and_1 (Output_0, not_1_out, Enable, not_2_out);
  and and_2 (Output_1, not_1_out, Enable, Input_b);
  and and_3 (Output_2, Input_a, Enable, not_2_out);
  and and_4 (Output_3, Input_a, Enable, Input_b);
endmodule

module Memory_cell (
  input  Select,
  input  Input,
  input  R_W,
  output Output
);

  wire and_1_out, and_2_out, not_1_out, not_2_out, sr_latch_1_output;

  not not_1 (not_1_out, Input);
  and and_1 (and_1_out, Select, not_2_out, not_1_out);
  and and_2 (and_2_out, Select, not_2_out, Input);
  not not_2 (not_2_out, R_W);
  SR_latch sr_latch_1 (.Set(and_1_out), .Reset(and_2_out), .Output(sr_latch_1_output));
  and and_3 (Output, Select, sr_latch_1_output, R_W);
endmodule

module SR_latch (
  input  Set,
  input  Reset,
  output Output
);

  wire nor_2_out;

  nor nor_1 (Output, Set, nor_2_out);
  nor nor_2 (nor_2_out, Output, Reset);
endmodule
