// Logisim project Registers.circ as structural Verilog
module Universal_shift_register (
  input  Clock,
  input  [1:0] Select,
  input  Shift_in_right,
  input  Shift_in_left,
  input  [15:0] Input,
  output [15:0] Output
);

  wire multiplexer_1_out, multiplexer_2_out, multiplexer_3_out, multiplexer_4_out, multiplexer_5_out,
       multiplexer_6_out, multiplexer_7_out, multiplexer_8_out, multiplexer_9_out, multiplexer_10_out,
       multiplexer_11_out, multiplexer_12_out, multiplexer_13_out, multiplexer_14_out, multiplexer_15_out,
       multiplexer_16_out;

  D_Flip_Flop d_ff_1 (.clk(Clock), .D(multiplexer_1_out), .Q(Output[15]));  // open: Qn, preset, en, reset
  Multiplexer #(.select(2), .disabled(0), .enable("false")) multiplexer_1 (
    .in0(Shift_in_right), .in1(1'b0), .in2(Input[15]), .in3(Output[14]), .out(multiplexer_1_out), .sel(Select));
  D_Flip_Flop d_ff_2 (.clk(Clock), .D(multiplexer_2_out), .Q(Output[14]));  // open: Qn, preset, en, reset
  Multiplexer #(.select(2), .disabled(0), .enable("false")) multiplexer_2 (
    .in0(Output[15]), .in1(1'b0), .in2(Input[14]), .in3(Output[13]), .out(multiplexer_2_out), .sel(Select));
  D_Flip_Flop d_ff_3 (.clk(Clock), .D(multiplexer_3_out), .Q(Output[13]));  // open: Qn, preset, en, reset
  Multiplexer #(.select(2), .disabled(0), .enable("false")) multiplexer_3 (
    .in0(Output[14]), .in1(1'b0), .in2(Input[13]), .in3(Output[12]), .out(multiplexer_3_out), .sel(Select));
  D_Flip_Flop d_ff_4 (.clk(Clock), .D(multiplexer_4_out), .Q(Output[12]));  // open: Qn, preset, en, reset
  Multiplexer #(.select(2), .disabled(0), .enable("false")) multiplexer_4 (
    .in0(Output[13]), .in1(1'b0), .in2(Input[12]), .in3(Output[11]), .out(multiplexer_4_out), .sel(Select));
  D_Flip_Flop d_ff_5 (.clk(Clock), .D(multiplexer_5_out), .Q(Output[11]));  // open: Qn, preset, en, reset
  Multiplexer #(.select(2), .disabled(0), .enable("false")) multiplexer_5 (
    .in0(Output[12]), .in1(1'b0), .in2(Input[11]), .in3(Output[10]), .out(multiplexer_5_out), .sel(Select));
  D_Flip_Flop d_ff_6 (.clk(Clock), .D(multiplexer_6_out), .Q(Output[10]));  // open: Qn, preset, en, reset
  Multiplexer #(.select(2), .disabled(0), .enable("false")) multiplexer_6 (
    .in0(Output[11]), .in1(1'b0), .in2(Input[10]), .in3(Output[9]), .out(multiplexer_6_out), .sel(Select));
  D_Flip_Flop d_ff_7 (.clk(Clock), .D(multiplexer_7_out), .Q(Output[9]));  // open: Qn, preset, en, reset
  Multiplexer #(.select(2), .disabled(0), .enable("false")) multiplexer_7 (
    .in0(Output[10]), .in1(1'b0), .in2(Input[9]), .in3(Output[8]), .out(multiplexer_7_out), .sel(Select));
  D_Flip_Flop d_ff_8 (.clk(Clock), .D(multiplexer_8_out), .Q(Output[8]));  // open: Qn, preset, en, reset
  Multiplexer #(.select(2), .disabled(0), .enable("false")) multiplexer_8 (
    .in0(Output[9]), .in1(1'b0), .in2(Input[8]), .in3(Output[7]), .out(multiplexer_8_out), .sel(Select));
  D_Flip_Flop d_ff_9 (.clk(Clock), .D(multiplexer_9_out), .Q(Output[7]));  // open: Qn, preset, en, reset
  Multiplexer #(.select(2), .disabled(0), .enable("false")) multiplexer_9 (
    .in0(Output[8]), .in1(1'b0), .in2(Input[7]), .in3(Output[6]), .out(multiplexer_9_out), .sel(Select));
  D_Flip_Flop d_ff_10 (.clk(Clock), .D(multiplexer_10_out), .Q(Output[6]));  // open: Qn, preset, en, reset
  Multiplexer #(.select(2), .disabled(0), .enable("false")) multiplexer_10 (
    .in0(Output[7]), .in1(1'b0), .in2(Input[6]), .in3(Output[5]), .out(multiplexer_10_out), .sel(Select));
  D_Flip_Flop d_ff_11 (.clk(Clock), .D(multiplexer_11_out), .Q(Output[5]));  // open: Qn, preset, en, reset
  Multiplexer #(.select(2), .disabled(0), .enable("false")) multiplexer_11 (
    .in0(Output[6]), .in1(1'b0), .in2(Input[5]), .in3(Output[4]), .out(multiplexer_11_out), .sel(Select));
  D_Flip_Flop d_ff_12 (.clk(Clock), .D(multiplexer_12_out), .Q(Output[4]));  // open: Qn, preset, en, reset
  Multiplexer #(.select(2), .disabled(0), .enable("false")) multiplexer_12 (
    .in0(Output[5]), .in1(1'b0), .in2(Input[4]), .in3(Output[3]), .out(multiplexer_12_out), .sel(Select));
  D_Flip_Flop d_ff_13 (.clk(Clock), .D(multiplexer_13_out), .Q(Output[3]));  // open: Qn, preset, en, reset
  Multiplexer #(.select(2), .disabled(0), .enable("false")) multiplexer_13 (
    .in0(Output[4]), .in1(1'b0), .in2(Input[3]), .in3(Output[2]), .out(multiplexer_13_out), .sel(Select));
  D_Flip_Flop d_ff_14 (.clk(Clock), .D(multiplexer_14_out), .Q(Output[2]));  // open: Qn, preset, en, reset
  Multiplexer #(.select(2), .disabled(0), .enable("false")) multiplexer_14 (
    .in0(Output[3]), .in1(1'b0), .in2(Input[2]), .in3(Output[1]), .out(multiplexer_14_out), .sel(Select));
  D_Flip_Flop d_ff_15 (.clk(Clock), .D(multiplexer_15_out), .Q(Output[1]));  // open: Qn, preset, en, reset
  Multiplexer #(.select(2), .disabled(0), .enable("false")) multiplexer_15 (
    .in0(Output[2]), .in1(1'b0), .in2(Input[1]), .in3(Output[0]), .out(multiplexer_15_out), .sel(Select));
  D_Flip_Flop d_ff_16 (.clk(Clock), .D(multiplexer_16_out), .Q(Output[0]));  // open: Qn, preset, en, reset
  Multiplexer #(.select(2), .disabled(0), .enable("false")) multiplexer_16 (
    .in0(Output[1]), .in1(1'b0), .in2(Input[0]), .in3(Shift_in_left), .out(multiplexer_16_out), .sel(Select));
endmodule
